# Fritzing sketch 08_Vibration Switch (saved by Fritzing 0.9.3b)
breadboards: 1

parts:
  module5 = Dule-Color LED
  module6 = Vibration Switch
  PART1 = Pi Wedge B+
  Raspberry_Pi_1 = Raspberry Pi 3 [part_number=RPI-3-V1.2]  # not connected

nets:
  N1: module5.G, PART1.GPIO_27, PART1.G27
  GND: module5.GND, module6.GND, PART1.GND
  N2: module5.R, PART1.G18
  N3: module6.SIG, PART1.GPIO_17, PART1.G17
  N4: module6.VCC, PART1.5V#71

notes:
  震动传感器
  双色LED灯

custom parts:
  Dule-Color LED: DuleColor LED module of SunFounder Sensor Kit
  Pi Wedge B+: This is the Pi Wedge B Plus, a board that connects to the Raspberry Pi B+’s 40-pin GPIO connector, and breaks the pins out to breadboard-friendly arrangement and spacing, and even adds a couple of decoupling capacitors on the power supply lines. The “Wedge” also makes the initial bringup process easier - you can plug an FTDI Basic module into the built-in serial port. Each Pi Wedge comes as an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
