# Fritzing sketch 12_Photo interrupter (saved by Fritzing 0.9.3b)
breadboards: 1

parts:
  PART1 = Pi Wedge B+
  Raspberry_Pi_1 = Raspberry Pi 3 [part_number=RPI-3-V1.2]  # not connected
  module6 = Photo-interrupter
  module7 = Dule-Color LED

nets:
  N1: PART1.5V#38, PART1.5V#71, module6.VCC
  N2: PART1.G17, module6.SIG
  GND: PART1.GND, module6.GND, module7.GND
  N3: PART1.G18, module7.R
  N4: PART1.G27, module7.G

notes:
  光隔离传感器
  双色LED灯

custom parts:
  Pi Wedge B+: This is the Pi Wedge B Plus, a board that connects to the Raspberry Pi B+’s 40-pin GPIO connector, and breaks the pins out to breadboard-friendly arrangement and spacing, and even adds a couple of decoupling capacitors on the power supply lines. The “Wedge” also makes the initial bringup process easier - you can plug an FTDI Basic module into the built-in serial port. Each Pi Wedge comes as an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
  Photo-interrupter: Photo-interrupter module of ZHIYU Sensor Kit
  Dule-Color LED: DuleColor LED module of SunFounder Sensor Kit
