# Fritzing sketch 13_PCF8591 (saved by Fritzing 0.9.3b)
breadboards: 1

parts:
  module5 = Dule-Color LED
  module6 = PCF8591
  PART1 = Pi Wedge B+
  Raspberry_Pi_1 = Raspberry Pi 3 [part_number=RPI-3-V1.2]  # not connected

nets:
  GND: module5.GND, module6.GND, PART1.GND
  N1: module5.R, module6.AO
  N2: module6.PM, module6.AIN0
  N3: module6.VCC, PART1.5V#71
  N4: module6.SDA, PART1.SDA
  N5: module6.SCL, PART1.SCL

notes:
  PCF8591
  双色LED灯
  调节PCF8591模块上的可调电阻，控制LED灯的亮度，可调电阻和AIN3脚关联。

custom parts:
  Dule-Color LED: DuleColor LED module of SunFounder Sensor Kit
  PCF8591: PCF8591 ADC module for SunFounder Sensor Kit
  Pi Wedge B+: This is the Pi Wedge B Plus, a board that connects to the Raspberry Pi B+’s 40-pin GPIO connector, and breaks the pins out to breadboard-friendly arrangement and spacing, and even adds a couple of decoupling capacitors on the power supply lines. The “Wedge” also makes the initial bringup process easier - you can plug an FTDI Basic module into the built-in serial port. Each Pi Wedge comes as an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
