# Fritzing sketch 14_Rain Detection (saved by Fritzing 0.9.3b)
breadboards: 1

parts:
  module13 = Rain Detection board
  module14 = LM393
  module15 = PCF8591
  PART1 = Pi Wedge B+
  Raspberry_Pi_1 = Raspberry Pi 3 [part_number=RPI-3-V1.2]  # not connected

nets:
  N1: module13.+, module14.GND#10
  N2: module13.-, module14.IN
  N3: module14.AO, module15.AIN0
  N4: module14.DO, PART1.G17
  VCC: module14.VCC, module15.VCC, PART1.5V#54
  GND: module14.GND#8, module15.GND, PART1.GND
  N5: module15.SDA, PART1.SDA
  N6: module15.SCL, PART1.SCL

notes:
  PCF8591
  雨滴传感器
  LM393模块

custom parts:
  Rain Detection board: Rain Detection board for ZHIYU Sensor Kit (along with LM393).
  LM393: LM393 module of ZHIYU Sensor Kit
  PCF8591: PCF8591 ADC module for SunFounder Sensor Kit
  Pi Wedge B+: This is the Pi Wedge B Plus, a board that connects to the Raspberry Pi B+’s 40-pin GPIO connector, and breaks the pins out to breadboard-friendly arrangement and spacing, and even adds a couple of decoupling capacitors on the power supply lines. The “Wedge” also makes the initial bringup process easier - you can plug an FTDI Basic module into the built-in serial port. Each Pi Wedge comes as an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
