# Fritzing sketch 15_JoyStick_PS2 (saved by Fritzing 0.9.3b)
breadboards: 1

parts:
  module11 = JoyStick
  module12 = PCF8591
  PART1 = Pi Wedge B+
  Raspberry_Pi_1 = Raspberry Pi 3 [part_number=RPI-3-V1.2]  # not connected

nets:
  GND: module11.GND, module12.GND, PART1.GND
  VCC: module11.VCC, module12.VCC, PART1.5V#54
  N1: module11.BT, module12.AIN2
  N2: module11.X, module12.AIN1
  N3: module11.Y, module12.AIN0
  N4: module12.SDA, PART1.SDA
  N5: module12.SCL, PART1.SCL

notes:
  PCF8591模块
  PS游戏手柄

custom parts:
  JoyStick: JoyStick module of ZHIYU Sensor Kit
  PCF8591: PCF8591 ADC module for SunFounder Sensor Kit
  Pi Wedge B+: This is the Pi Wedge B Plus, a board that connects to the Raspberry Pi B+’s 40-pin GPIO connector, and breaks the pins out to breadboard-friendly arrangement and spacing, and even adds a couple of decoupling capacitors on the power supply lines. The “Wedge” also makes the initial bringup process easier - you can plug an FTDI Basic module into the built-in serial port. Each Pi Wedge comes as an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
