# Fritzing sketch 16_Potentiometer (saved by Fritzing 0.9.3b)
circuit board: 8.46667cm x 5.64444cm
breadboards: 1

parts:
  module16 = Dule-Color LED
  module17 = Potentiometer
  module18 = PCF8591
  PART1 = Pi Wedge B+
  Raspberry_Pi_1 = Raspberry Pi 3 [part_number=RPI-3-V1.2]  # not connected

nets:
  GND: module16.GND, module17.GND, module18.GND, PART1.GND
  N1: module16.R, module18.AO
  N2: module17.SIG, module18.AIN0
  VCC: module17.VCC, module18.VCC, PART1.5V#54
  N3: module18.SDA, PART1.GPIO_2_(I2C1_SDA), PART1.SDA
  N4: module18.SCL, PART1.GPIO_3_(I2C1_SCL), PART1.SCL

notes:
  PCF8591模块
  电位器模块
  双色LED灯

custom parts:
  Dule-Color LED: DuleColor LED module of SunFounder Sensor Kit
  Potentiometer: Potentiometer module of ZHIYU Sensor Kit
  PCF8591: PCF8591 ADC module for SunFounder Sensor Kit
  Pi Wedge B+: This is the Pi Wedge B Plus, a board that connects to the Raspberry Pi B+’s 40-pin GPIO connector, and breaks the pins out to breadboard-friendly arrangement and spacing, and even adds a couple of decoupling capacitors on the power supply lines. The “Wedge” also makes the initial bringup process easier - you can plug an FTDI Basic module into the built-in serial port. Each Pi Wedge comes as an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
