# Fritzing sketch 19_Sound Sensor (saved by Fritzing 0.9.3b)
breadboards: 1

parts:
  module15 = PCF8591
  PART1 = Pi Wedge B+
  Raspberry_Pi_1 = Raspberry Pi 3 [part_number=RPI-3-V1.2]  # not connected
  module17 = Sound Sensor

nets:
  N1: module15.AIN0, module17.SIG
  VCC: module15.VCC, PART1.5V#54, module17.VCC
  GND: module15.GND, PART1.GND, module17.GND
  N2: module15.SDA, PART1.SDA
  N3: module15.SCL, PART1.SCL

notes:
  PCF8591
  声音传感器

custom parts:
  PCF8591: PCF8591 ADC module for SunFounder Sensor Kit
  Pi Wedge B+: This is the Pi Wedge B Plus, a board that connects to the Raspberry Pi B+’s 40-pin GPIO connector, and breaks the pins out to breadboard-friendly arrangement and spacing, and even adds a couple of decoupling capacitors on the power supply lines. The “Wedge” also makes the initial bringup process easier - you can plug an FTDI Basic module into the built-in serial port. Each Pi Wedge comes as an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
  Sound Sensor: Sound Sensor module of ZHIYU Sensor Kit
