# Fritzing sketch 22_Gas Sensor (saved by Fritzing 0.9.3b)
breadboards: 1

parts:
  module23 = MQ-2 Gas Sensor
  module24 = PCF8591
  PART1 = Pi Wedge B+
  module25 = Buzzer

nets:
  N1: module23.AO, module24.AIN0
  N2: module23.DO, PART1.G17
  N3: module23.VCC, PART1.5V#39, PART1.5V#71
  GND: module23.GND, module24.GND, PART1.GND, module25.GND
  VCC: module24.VCC, PART1.3.3V#19, PART1.3.3V#55, module25.VCC
  N4: module24.SDA, PART1.SDA
  N5: module24.SCL, PART1.SCL
  N6: PART1.G18, module25.SIG

notes:
  PCF8591
  Gas Sensor
  Active Buzzer

custom parts:
  MQ-2 Gas Sensor: MQ-2 Gas Sensor module of ZHIYU Sensor Kit
  PCF8591: PCF8591 ADC module for SunFounder Sensor Kit
  Pi Wedge B+: This is the Pi Wedge B Plus, a board that connects to the Raspberry Pi B+’s 40-pin GPIO connector, and breaks the pins out to breadboard-friendly arrangement and spacing, and even adds a couple of decoupling capacitors on the power supply lines. The “Wedge” also makes the initial bringup process easier - you can plug an FTDI Basic module into the built-in serial port. Each Pi Wedge comes as an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
  Buzzer: Buzzer module of ZHIYU Sensor Kit
