# Fritzing sketch 24_Touch_Switch (saved by Fritzing 0.9.3b)
breadboards: 1

parts:
  module6 = Touch Switch
  module7 = Dule-Color LED
  PART1 = Pi Wedge B+
  Raspberry_Pi_1 = Raspberry Pi 3 [part_number=RPI-3-V1.2]  # not connected

nets:
  N1: module6.SIG, PART1.G17
  GND: module6.GND, module7.GND, PART1.GND
  N2: module6.VCC, PART1.5V#71
  N3: module7.G, PART1.GPIO_27, PART1.G27
  N4: module7.R, PART1.GPIO_18, PART1.G18

notes:
  Touch Switch
  双色LED灯

custom parts:
  Touch Switch: Touch Switch module of ZHIYU Sensor Kit
  Dule-Color LED: DuleColor LED module of SunFounder Sensor Kit
  Pi Wedge B+: This is the Pi Wedge B Plus, a board that connects to the Raspberry Pi B+’s 40-pin GPIO connector, and breaks the pins out to breadboard-friendly arrangement and spacing, and even adds a couple of decoupling capacitors on the power supply lines. The “Wedge” also makes the initial bringup process easier - you can plug an FTDI Basic module into the built-in serial port. Each Pi Wedge comes as an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
