# Fritzing sketch 25_Ultrasonic_Ranging (saved by Fritzing 0.9.3b)
breadboards: 1

parts:
  ZHIYU1 = 超声波传感器
  PART1 = Pi Wedge B+
  Raspberry_Pi_1 = Raspberry Pi 3 [part_number=RPI-3-V1.2]  # not connected

nets:
  N1: ZHIYU1.VCC, PART1.5V#38, PART1.5V#71
  N2: ZHIYU1.Trig, PART1.G17
  N3: ZHIYU1.Echo, PART1.G18
  GND: ZHIYU1.GND, PART1.GND

notes:
  超声波传感器模块

custom parts:
  超声波传感器: ZHIYU Server
  Pi Wedge B+: This is the Pi Wedge B Plus, a board that connects to the Raspberry Pi B+’s 40-pin GPIO connector, and breaks the pins out to breadboard-friendly arrangement and spacing, and even adds a couple of decoupling capacitors on the power supply lines. The “Wedge” also makes the initial bringup process easier - you can plug an FTDI Basic module into the built-in serial port. Each Pi Wedge comes as an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
